# Fritzing sketch Satu Sensor (saved by Fritzing 1.0.1rc)
breadboards: 1

parts:
  A1 = ESP32 DevKitc V4
  M1 = fc-51 [package=THT]
  LED1 = RGB LED (com. cathode, rgb) [package="5 mm [THT]"]  # not connected

nets:
  N1: A1.Pin_8, M1.pin1
  N2: A1.Pin_14, A1.Pin_38, M1.pin2
  N3: A1.Pin_19, M1.pin3

custom parts:
  ESP32 DevKitc V4: ESP32-DevKitC board with ESP32-WROOM-32 module. ESP32-DevKitC V4 is a small-sized ESP32-based development board produced by Espressif. Most of the pins on the ESP module are broken out to the pin headers on the board. The pins D0, D1, D2, D3, CMD and CLK are used internally for communication between ESP32 and SPI flash memory. They are grouped on both sides near the USB connector. Avoid using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
